# Fritzing sketch thermostat (saved by Fritzing 0.8.3b)
breadboards: 1

parts:
  Part1 = Arduino Uno (Rev3)
  CC3K1 = Adafruit CC3000 WiFi Breakout
  DHT1 = DHT11 Humitidy and Temperature Sensor
  R1 = Resistor [tolerance=±5% resistance=10k package=THT]

nets:
  GND: Part1.GND, CC3K1.GND, DHT1.GND
  N1: Part1.D10_PWM/SS, CC3K1.CS
  N2: Part1.D11_PWM/MOSI, CC3K1.MOSI
  N3: Part1.D12/MISO, CC3K1.MISO
  N4: Part1.D13/SCK, CC3K1.CLK
  N5: Part1.D2, DHT1.DATA, R1.Pin_1
  N6: Part1.D3_PWM, CC3K1.IRQ
  N7: Part1.D5_PWM, CC3K1.VBEN
  5V: Part1.5V, CC3K1.VIN, DHT1.VDD, R1.Pin_0

custom parts:
  Adafruit CC3000 WiFi Breakout: CC3000 WiFi Breakout
  DHT11 Humitidy and Temperature Sensor: DHT11 Humidity and Temperature Sensor
